# Fritzing sketch AlarmClock (saved by Fritzing 0.9.2b)
breadboards: 2

parts:
  Part1 = Arduino Uno (Rev3)
  IC2 = DS1302 [package="DIP8 [THT]"]
  BAT2 = Battery Holders [package=battcon_12mm]
  LCD2 = LCD screen
  Part2 = RFID-RC522-v2
  J1 = Piezo Speaker
  S1 = Momentary Switch [package=ksa_sealed_tac_switch]
  S2 = Momentary Switch [package=ksa_sealed_tac_switch]
  S3 = Momentary Switch [package=ksa_sealed_tac_switch]

nets:
  N1: Part1.A4/SDA, LCD2.SDA
  N2: Part1.A5/SCL, LCD2.SCL
  N3: Part1.D8, S1.4
  N4: Part1.D9_PWM, J1.pin2
  N5: Part1.D10_PWM/SS, Part2.SDA
  N6: Part1.D11_PWM/MOSI, Part2.MOSI
  N7: Part1.D12/MISO, Part2.MISO
  N8: Part1.D13/SCK, Part2.SCK
  N9: Part1.D2, S3.4
  N10: Part1.D3_PWM, Part2.RST
  N11: Part1.D4, S2.4
  N12: Part1.D5_PWM, IC2.CE_-_Chip_Enable
  N13: Part1.D6_PWM, IC2.I/O_-_SPI_Data_In/Out
  N14: Part1.D7, IC2.SCLK_-_SPI_Clock
  3V3: Part1.3V3, Part2.3.3V
  5V: Part1.5V, IC2.+V, LCD2.VCC
  GND: Part1.GND, IC2.X2_-_Crystal, IC2.0V, BAT2.-, LCD2.GND, Part2.GND, J1.pin1, S3.2
  N15: IC2.Vbat_-_Backup_Supply, BAT2.+
  N16: LCD2.LED+, LCD2.LED-

custom parts:
  LCD screen: A standard character display, usually with 2x16 characters. Comes in many colors.
  RFID-RC522-v2: A simple China made RFID-RC522 Reader; do check the pin labels, as this is a MFRC522 based clone.
